// Logisim project 1bitFullAdd.circ as structural Verilog: 1 circuit, main circuit main
module main (
  input  initial_s,
  input  y,
  input  in_3,
  output c,
  output s
);

  wire and_1_out, and_2_out, main_1_out_3;

  xor_main main_1 (.in_1(initial_s), .in_2(y), .out_3(main_1_out_3));
  and and_1 (and_1_out, initial_s, y);
  xor_main main_2 (.in_1(main_1_out_3), .in_2(in_3), .out_3(s));
  and and_2 (and_2_out, main_1_out_3, in_3);
  or or_1 (c, and_1_out, and_2_out);

  // Notes on the sheet:
  //   x
  //   Input.carry
  //   A map of UMM
endmodule
