// Logisim project 1bitHalfAdd.circ as structural Verilog: 1 circuit, main circuit main
module main (
  input  x,
  input  y,
  output c,
  output s
);

  xor_main main_1 (.in_1(x), .in_2(y), .out_3(s));
  and and_1 (c, x, y);
endmodule
