// Logisim project 2bitAddition.circ as structural Verilog: 1 circuit, main circuit main
module main (
  input  in_1,
  input  bit_1,
  input  in_3,
  input  bit_0,
  input  carry,
  output out_6,
  output out_7,
  output out_8
);

  wire main_2_c;

  _1bitFullAdd_main main_1 (.initial_s(in_1), .y(bit_1), .in_3(main_2_c), .c(out_6), .s(out_7));
  _1bitFullAdd_main main_2 (.initial_s(in_3), .y(bit_0), .in_3(carry), .c(main_2_c), .s(out_8));

  // Notes on the sheet:
  //   y
  //   x
  //   z
endmodule
