// Logisim project 32bitAddition.circ as structural Verilog: 1 circuit, main circuit main
module main (
  input  in_1,
  input  in_2,
  input  in_3,
  input  in_4,
  input  in_5,
  input  in_6,
  input  in_7,
  input  in_8,
  input  in_9,
  input  in_10,
  input  in_11,
  input  in_12,
  input  in_13,
  input  in_14,
  input  in_15,
  input  in_16,
  input  in_17,
  input  in_18,
  input  in_19,
  input  in_20,
  input  in_21,
  input  in_22,
  input  in_23,
  input  in_24,
  input  in_25,
  input  in_26,
  input  in_27,
  input  in_28,
  input  in_29,
  input  in_30,
  input  in_31,
  input  in_32,
  input  in_33,
  input  in_34,
  input  in_35,
  input  in_36,
  input  in_37,
  input  in_38,
  input  in_39,
  input  in_40,
  input  in_41,
  input  in_42,
  input  in_43,
  input  in_44,
  input  in_45,
  input  in_46,
  input  in_47,
  input  in_48,
  input  in_49,
  input  in_50,
  input  in_51,
  input  in_52,
  input  in_53,
  input  in_54,
  input  in_55,
  input  in_56,
  input  in_57,
  input  in_58,
  input  in_59,
  input  in_60,
  input  in_61,
  input  in_62,
  input  in_63,
  input  in_64,
  input  in_65,
  output out_66,
  output out_67,
  output out_68,
  output out_69,
  output out_70,
  output out_71,
  output out_72,
  output out_73,
  output out_74,
  output out_75,
  output out_76,
  output out_77,
  output out_78,
  output out_79,
  output out_80,
  output out_81,
  output out_82,
  output out_83,
  output out_84,
  output out_85,
  output out_86,
  output out_87,
  output out_88,
  output out_89,
  output out_90,
  output out_91,
  output out_92,
  output out_93,
  output out_94,
  output out_95,
  output out_96,
  output out_97,
  output out_98
);

  wire main_2_out_34;

  _16bitAddition_main main_1 (
    .in_1(in_1), .in_2(in_2), .in_3(in_3), .in_4(in_4), .in_5(in_5), .in_6(in_6), .in_7(in_7), .in_8(in_8),
    .in_9(in_9), .in_10(in_10), .in_11(in_11), .in_12(in_12), .in_13(in_13), .in_14(in_14), .in_15(in_15),
    .in_16(in_16), .in_17(in_17), .in_18(in_18), .in_19(in_19), .in_20(in_20), .in_21(in_21), .in_22(in_22),
    .in_23(in_23), .in_24(in_24), .in_25(in_25), .in_26(in_26), .in_27(in_27), .in_28(in_28), .in_29(in_29),
    .in_30(in_30), .in_31(in_31), .in_32(in_32), .in_33(main_2_out_34), .out_34(out_66), .out_35(out_67),
    .out_36(out_68), .out_37(out_69), .out_38(out_70), .out_39(out_71), .out_40(out_72), .out_41(out_73),
    .out_42(out_74), .out_43(out_75), .out_44(out_76), .out_45(out_77), .out_46(out_78), .out_47(out_79),
    .out_48(out_80), .out_49(out_81), .out_50(out_82));
  _16bitAddition_main main_2 (
    .in_1(in_33), .in_2(in_34), .in_3(in_35), .in_4(in_36), .in_5(in_37), .in_6(in_38), .in_7(in_39),
    .in_8(in_40), .in_9(in_41), .in_10(in_42), .in_11(in_43), .in_12(in_44), .in_13(in_45), .in_14(in_46),
    .in_15(in_47), .in_16(in_48), .in_17(in_49), .in_18(in_50), .in_19(in_51), .in_20(in_52), .in_21(in_53),
    .in_22(in_54), .in_23(in_55), .in_24(in_56), .in_25(in_57), .in_26(in_58), .in_27(in_59), .in_28(in_60),
    .in_29(in_61), .in_30(in_62), .in_31(in_63), .in_32(in_64), .in_33(in_65), .out_34(main_2_out_34),
    .out_35(out_83), .out_36(out_84), .out_37(out_85), .out_38(out_86), .out_39(out_87), .out_40(out_88),
    .out_41(out_89), .out_42(out_90), .out_43(out_91), .out_44(out_92), .out_45(out_93), .out_46(out_94),
    .out_47(out_95), .out_48(out_96), .out_49(out_97), .out_50(out_98));
endmodule
