// Logisim project 41mux.circ as structural Verilog: 1 circuit, main circuit main
module main (
  input  x0,
  input  x1,
  input  x2,
  input  x3,
  input  s,
  input  in_6,
  output out_7
);

  wire _21mux_y, main_1_y, main_2_out_3;

  _21mux_main main_1 (.x0(x0), .selector(s), .x1(x1), .y(main_1_y));
  _21mux_main _21mux (.x0(x2), .selector(in_6), .x1(x3), .y(_21mux_y));
  xor_main main_2 (.in_1(s), .in_2(in_6), .out_3(main_2_out_3));
  _21mux_main main_3 (.x0(main_1_y), .selector(main_2_out_3), .x1(_21mux_y), .y(out_7));

  // Notes on the sheet:
  //   21mux
  //   xor
  //   21mux
endmodule
