// Logisim project 4bitAddition.circ as structural Verilog: 1 circuit, main circuit main
module main (
  input  bit_3,
  input  in_2,
  input  bit_2,
  input  in_4,
  input  bit_1,
  input  in_6,
  input  bit_0,
  input  in_8,
  input  carry_bit,
  output out_10,
  output out_11,
  output out_12,
  output out_13,
  output out_14
);

  wire main_2_out_6;

  _2bitAddition_main main_1 (
    .in_1(bit_3), .bit_1(in_2), .in_3(bit_2), .bit_0(in_4), .carry(main_2_out_6), .out_6(out_10),
    .out_7(out_11), .out_8(out_12));
  _2bitAddition_main main_2 (
    .in_1(bit_1), .bit_1(in_6), .in_3(bit_0), .bit_0(in_8), .carry(carry_bit), .out_6(main_2_out_6),
    .out_7(out_13), .out_8(out_14));

  // Notes on the sheet:
  //   y
  //   x
  //   z
endmodule
