// Logisim project 8bitAddition.circ as structural Verilog: 1 circuit, main circuit main
module main (
  input  in_1,
  input  in_2,
  input  in_3,
  input  in_4,
  input  in_5,
  input  in_6,
  input  in_7,
  input  in_8,
  input  in_9,
  input  in_10,
  input  in_11,
  input  in_12,
  input  in_13,
  input  in_14,
  input  in_15,
  input  in_16,
  input  in_17,
  output out_18,
  output out_19,
  output out_20,
  output out_21,
  output out_22,
  output out_23,
  output out_24,
  output out_25,
  output out_26
);

  wire main_2_out_10;

  _4bitAddition_main main_1 (
    .bit_3(in_1), .in_2(in_2), .bit_2(in_3), .in_4(in_4), .bit_1(in_5), .in_6(in_6), .bit_0(in_7),
    .in_8(in_8), .carry_bit(main_2_out_10), .out_10(out_18), .out_11(out_19), .out_12(out_20),
    .out_13(out_21), .out_14(out_22));
  _4bitAddition_main main_2 (
    .bit_3(in_9), .in_2(in_10), .bit_2(in_11), .in_4(in_12), .bit_1(in_13), .in_6(in_14), .bit_0(in_15),
    .in_8(in_16), .carry_bit(in_17), .out_10(main_2_out_10), .out_11(out_23), .out_12(out_24),
    .out_13(out_25), .out_14(out_26));
endmodule
