// Logisim project GatedDLatch.circ as structural Verilog: 1 circuit, main circuit main
module main (
  input  in_1,
  input  in_2,
  output out_3,
  output out_4
);

  wire and_1_out, and_2_out, and_3_out, and_4_out, not_1_out, not_2_out;

  and and_1 (and_1_out, in_1, in_2);
  and and_2 (and_2_out, not_1_out, in_2);
  not not_1 (not_1_out, and_1_out);
  not not_2 (not_2_out, and_2_out);
  not not_3 (out_3, and_3_out);
  and and_3 (and_3_out, not_1_out, out_4);
  and and_4 (and_4_out, out_3, not_2_out);
  not not_4 (out_4, and_4_out);
endmodule
